# Fritzing sketch sketch (saved by Fritzing 1.0.1rc)
breadboards: 1

parts:
  Part1 = Arduino Pro Mini v13
  U1 = USB_AB [package=usb-ab-micro-smd]
  IR1 = TSOP312.., 314.. [package=THT]
  LED1 = LEDs [package=led10mm]
  LED2 = LEDs [package=led10mm]

nets:
  GND: Part1.GND, U1.D-, IR1.GND, LED2.C
  N1: Part1.VCC, IR1.Vs
  N2: Part1.D3_PWM, LED1.A
  N3: Part1.D2, IR1.Data
  N4: LED1.C, LED2.A
